# Fritzing sketch lightbulb (saved by Fritzing 0.9.1b)
breadboards: 1

parts:
  J1_/_i2c = female pin header, 2 pins [form="♀ (female)"]
  TSL2561 = _TL2561
  MCU = Pro Trinket 3.3V
  LED1 = smd LED [color="Red (633nm)" package="1206 [SMD]"]
  R1 = Resistor [tolerance=±5% resistance=330 package=THT]
  RF433MHZ = RF-LINK_TX [package=rf-link_tx]

nets:
  N1: J1_/_i2c.pin1, TSL2561.SCL, MCU.A5
  N2: J1_/_i2c.pin2, TSL2561.SDA, MCU.A4
  GND: TSL2561.GND, MCU.GND, R1.Pin_1, RF433MHZ.GND
  3.3V: MCU.+3V3
  N3: MCU.D3, RF433MHZ.DATA
  N4: MCU.D11, LED1.anode
  N5: LED1.cathode, R1.Pin_0
  9V: RF433MHZ.+12V

notes:
  Light bulb device / i2c device

custom parts:
  : Sensor de Luminosidade - TL2561
  Pro Trinket 3.3V: The Pro Trinket 3.3V is like an Arduino Pro Mini with more pins and USB included. However, it uses 3V logic and 12MHz clock which means it's good when you want a lower-power and lower-voltage setup. Built with the common core Arduino chip, the ATmega328p, it has 18 GPIO, 2 extra analog inputs, 28K of flash, and 2K of RAM. It has onboard USB bootloading support with Optiboot support, so you can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
  RF-LINK_TX: RF Link transmitters WRL-8945, 8946
