# Fritzing sketch weatherstation (saved by Fritzing 0.9.1b)
breadboards: 1

parts:
  J1_/_i2c = female pin header, 2 pins [form="♀ (female)"]
  TSL2561 = _TL2561
  MCU = Pro Trinket 3.3V
  BME280 = _TL2561
  MCP9808 = _TL2561
  TCS34725 = _TL2561

nets:
  N1: J1_/_i2c.pin1, TSL2561.SCL, MCU.A5, BME280.SCL, MCP9808.SCL, TCS34725.SCL
  N2: J1_/_i2c.pin2, TSL2561.SDA, MCU.A4, BME280.SDA, MCP9808.SDA, TCS34725.SDA
  GND: TSL2561.GND, MCU.GND, BME280.GND, MCP9808.GND, TCS34725.GND
  5V: TSL2561.Vcc, BME280.Vcc, MCP9808.Vcc, TCS34725.Vcc
  3.3V: MCU.+3V3

notes:
  Weather station/ i2c device

custom parts:
  : Sensor de Luminosidade - TL2561
  Pro Trinket 3.3V: The Pro Trinket 3.3V is like an Arduino Pro Mini with more pins and USB included. However, it uses 3V logic and 12MHz clock which means it's good when you want a lower-power and lower-voltage setup. Built with the common core Arduino chip, the ATmega328p, it has 18 GPIO, 2 extra analog inputs, 28K of flash, and 2K of RAM. It has onboard USB bootloading support with Optiboot support, so you can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
